# Fritzing sketch esp32RFID (saved by Fritzing 0.9.2b)

parts:
  Part1 = RFID-RC522-v2
  U1 = ESP32S-HiLetgo [part_number=ESP32S-HiLetgo]

nets:
  N1: Part1.SDA, U1.GPIO5
  N2: Part1.SCK, U1.GPIO18
  N3: Part1.MOSI, U1.GPIO23
  N4: Part1.MISO, U1.GPIO19
  GND: Part1.GND, U1.GND
  N5: Part1.RST, U1.GPIO27
  N6: Part1.3.3V, U1.3.3

notes:
  sda | G5
  sck | G18
  mosi | G32
  miso | G19
  3.3v | 3.3v
  rst | G27
  gnd | gnd

custom parts:
  RFID-RC522-v2: A simple China made RFID-RC522 Reader; do check the pin labels, as this is a MFRC522 based clone.
  ESP32S-HiLetgo: HiLetgo ESP-WROOM-32 ESP32 ESP-32S Development Board 2.4GHz Dual-Mode WiFi + Bluetooth Dual Cores Microcontroller The ESP32 integrated with Antenna switches, RF Balun, power amplifiers, low-noise amplifiers, filters, and management modules, and the entire solution occupies the least area of PCB. 2.4 GHz Wi-Fi plus Bluetooth dual-mode chip, with TSMC Ultra-low power consumption 40nm technology,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
